# Fritzing sketch Ascensor (saved by Fritzing 0.9.3b)
breadboards: 1

parts:
  M1 = DC Motor  # not connected
  S1 = H-Bridge with L298N
  BUTTON1 = Arcade Button (pink)
  HC-SR04_Sensor_1 = HC-SR04 Ultrasonic Distance Sensor
  Componente1 = Arduino Uno (Rev3)
  BATT1 = 4xAA Switchable Battery Pack w/Bare Wire
  Componente2 = LCD1602-I2C

nets:
  N1: S1.12V, BATT1.POS
  GND: S1.GND, HC-SR04_Sensor_1.GND, Componente1.GND, BATT1.NEG, Componente2.GND
  5V: S1.5V, BUTTON1.no_name_yet#2, HC-SR04_Sensor_1.VCC, Componente1.5V, Componente2.VCC
  N2: S1.ENA, Componente1.D11_PWM/MOSI
  N3: S1.IN1, Componente1.D13/SCK
  N4: S1.IN2, Componente1.D12/MISO
  N5: BUTTON1.no_name_yet#1, Componente1.D10_PWM/SS
  N6: HC-SR04_Sensor_1.TRIG, Componente1.D4
  N7: HC-SR04_Sensor_1.ECHO, Componente1.D2
  N8: Componente1.A4/SDA, Componente2.SDA
  N9: Componente1.A5/SCL, Componente2.SCL

notes:
  1a Planta

custom parts:
  H-Bridge with L298N: h-bridge
  Arcade Button (pink): Adafruit Arcade Button (pink)
  4xAA Switchable Battery Pack w/Bare Wire: 4xAA Switchable Battery Pack with Bare Wire connection
  LCD1602-I2C: A standard character display, usually with 2x16 characters. Comes in many colors with LCM1602 IIC attached.
